# Fritzing sketch Wetterstation (saved by Fritzing 1.0.1rc)
breadboards: 1

parts:
  Mod1 = Amica NodeMCU DEVKIT 1.0
  DHT1 = DHT22 Humidity and Temperature Sensor
  Bauteil1 = Adafruit TSL2561 [part_number="Adafruit #439"]
  Bauteil2 = VEML6070 [part_number=VEML6070]
  Bauteil3 = Soil Moisture Sensor
  Bauteil6 = GY-BMEP280 Barometric Pressure Sensor - Breakout

nets:
  VDD: Mod1.pin1, Mod1.pin_10, Mod1.pin_26, DHT1.VDD, Bauteil1.3.3V, Bauteil2.VDD, Bauteil3.VCC, Bauteil6.VCC
  GND: Mod1.pin2, Mod1.pin_9, Mod1.pin_25, Mod1.pin_29, DHT1.GND, Bauteil1.GND, Bauteil2.GND, Bauteil3.GND, Bauteil6.GND

custom parts:
  Adafruit TSL2561: The TSL2561 luminosity sensor is an advanced digital light sensor, ideal for use in a wide range of light situations. Compared to low cost CdS cells, this sensor is more precise, allowing for exact lux calculations and can be configured for different gain/timing ranges to detect light ranges from up to 0.1 - 40,000+ Lux on the fly. The best part of this sensor is that it contains both infrared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
  VEML6070: This little sensor is a great way to add UV light sensing to any microcontroller project. The VEML6070 from Vishay has a true UV A light sensor and an I2C-controlled ADC that will take readings and integrate them for you over ~60ms to 500ms.
  GY-BMEP280 Barometric Pressure Sensor - Breakout: The BME280 is a chip which was originally designed for the next generation of smartphones. It is made up of a very accurate pressure sensor and an associated temperature sensor which helps calibrate the pressure readings. And just for fun they threw in a pretty solid humidity sensor in there as well! So with an I2C connection you have access to enough weather data to make some pretty good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
